# Fritzing sketch schema_elettrico_tovaglietta (saved by Fritzing 0.8.7b)
circuit board: 8.46667cm x 5.64444cm
perfboards: 1

parts:
  R2 = Resistor [tolerance=±5% resistance=330k package=THT]
  R4 = Resistor [tolerance=±5% resistance=330k package=THT]
  R5 = Resistor [tolerance=±5% resistance=330k package=THT]
  R7 = Resistor [tolerance=±5% resistance=330k package=THT]
  R8 = Resistor [tolerance=±5% resistance=330k package=THT]
  R9 = Resistor [tolerance=±5% resistance=330k package=THT]
  R10 = Resistor [tolerance=±5% resistance=18k package=THT]
  R11 = Resistor [tolerance=±5% resistance=18k package=THT]
  R12 = Resistor [tolerance=±5% resistance=18k package=THT]
  R13 = Resistor [tolerance=±5% resistance=18k package=THT]
  R15 = Resistor [tolerance=±5% resistance=18k package=THT]
  R16 = Resistor [tolerance=±5% resistance=18k package=THT]
  R17 = Resistor [tolerance=±5% resistance=18k package=THT]
  R18 = Resistor [tolerance=±5% resistance=18k package=THT]
  R19 = Resistor [tolerance=±5% resistance=330k package=THT]
  R6 = Resistor [tolerance=±5% resistance=330k package=THT]
  R3 = Resistor [tolerance=±5% resistance=330k package=THT]
  R14 = Resistor [tolerance=±5% resistance=18k package=THT]
  Componente1 = Arduino Uno (Rev3)

nets:
  N1: R2.Pin_0, R4.Pin_0, R5.Pin_0, R7.Pin_0, R8.Pin_0, R9.Pin_0, R19.Pin_0, R6.Pin_0, R3.Pin_0, Componente1.5V
  N2: R2.Pin_1, R11.Pin_0
  N3: R4.Pin_1, R13.Pin_0
  N4: R5.Pin_1, R14.Pin_0
  N5: R7.Pin_1, R16.Pin_0
  N6: R8.Pin_1, R17.Pin_0
  N7: R9.Pin_1, R18.Pin_0
  N8: R10.Pin_0, R19.Pin_1
  N9: R10.Pin_1, Componente1.A0
  N10: R11.Pin_1, Componente1.D9_PWM
  N11: R12.Pin_0, R3.Pin_1
  N12: R12.Pin_1, Componente1.D8
  N13: R13.Pin_1, Componente1.D5_PWM
  N14: R15.Pin_0, R6.Pin_1
  N15: R15.Pin_1, Componente1.A4/SDA
  N16: R16.Pin_1, Componente1.A3
  N17: R17.Pin_1, Componente1.A2
  N18: R18.Pin_1, Componente1.A1
  N19: R14.Pin_1, Componente1.A5/SCL

notes:
  sensore8
  sensore1
  sensore2
  sensore3
  sensore4
  sensore5
  sensore6
  sensore7
  sensore9
